# Fritzing sketch schematic (saved by Fritzing 0.9.3b)
perfboards: 1

parts:
  WeMos_D1_Mini1 = WeMos D1 Mini
  WPS = Pushbutton [package="[SMD]"]
  LED_STRIP = female pin header, 4 pins [form="♀ (female)"]
  BLUE = MOSFET-NCHANNEL [part_number=TN0610 package=to-92]
  RED = MOSFET-NCHANNEL [part_number=TN0610 package=to-92]
  GREEN = MOSFET-NCHANNEL [part_number=TN0610 package=to-92]

nets:
  N1: WeMos_D1_Mini1.5V, LED_STRIP.pin1
  N2: WeMos_D1_Mini1.D1, RED.G
  N3: WeMos_D1_Mini1.D2, GREEN.G
  N4: WeMos_D1_Mini1.D3, BLUE.G
  N5: WeMos_D1_Mini1.D5, WPS.Pin_3, WPS.Pin_4
  N6: WeMos_D1_Mini1.G, WPS.Pin_1, WPS.Pin_2, BLUE.S, RED.S, GREEN.S
  N7: LED_STRIP.pin2, GREEN.D
  N8: LED_STRIP.pin3, RED.D
  N9: LED_STRIP.pin4, BLUE.D

custom parts:
  MOSFET-NCHANNEL: Generic NMOS footprint
